# Fritzing sketch Attached to drone (saved by Fritzing 0.9.2b)

parts:
  PART1 = ML8511 UV Sensor Breakout [part_number=SEN-12705]
  Part1 = Arduino Uno (Rev3)
  RHT1 = Humidity and Temperature Sensor RHT03
  U1 = RF-LINK_TX [package=rf-link_tx]
  Part2 = Barometric Pressure Sensor - BMP085 Breakout
  ANT1 = Antenna

nets:
  3.3V: PART1.EN, PART1.3.3V, Part1.3V3, Part2.VCC
  N1: PART1.OUT, Part1.A0
  GND: PART1.GND, Part1.GND, RHT1.GND_2, U1.GND, Part2.GND
  N2: Part1.A4/SDA, Part2.SDA
  N3: Part1.A5/SCL, Part2.SCL
  N4: Part1.D2, RHT1.Data-signal
  N5: Part1.D3_PWM, U1.DATA
  5V: Part1.5V, RHT1.Vcc, U1.+5V
  N6: U1.ANT, ANT1.antenna_lead

custom parts:
  ML8511 UV Sensor Breakout: Description: The ML8511 breakout is an easy to use ultraviolet light sensor. The MP8511 UV Sensor works by outputing an analog signal in relation to the amount of UV light it detects. This breakout can be very handy in creating devices that warn the user of sunburn or detect the UV index as it relates to weather conditions. This sensor breakout can detect 280-390nm light most effectively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
