# Fritzing sketch attached to computer (saved by Fritzing 0.9.2b)

parts:
  Part1 = Arduino Uno (Rev3)
  U1 = RF-LINK_TX [package=rf-link_tx]
  ANT1 = Antenna

nets:
  N1: Part1.D2, U1.DATA
  5V: Part1.5V, U1.+5V
  GND: Part1.GND, U1.GND
  N2: U1.ANT, ANT1.antenna_lead
